// Logisim project 74HC.circ as structural Verilog: 12 circuits, main circuit EightBitLatch
// 74HC377
module EightBitLatch (
  input  [7:0] D,
  input  EN_LO,
  input  CP_RE,
  output [7:0] Y
);

  wire and_1_out, and_2_out, and_3_out, and_4_out, and_5_out, and_6_out, and_7_out, and_8_out, and_9_out,
       and_10_out, and_11_out, and_12_out, and_13_out, and_14_out, and_15_out, and_16_out, not_1_out,
       not_2_out, not_3_out, not_4_out, not_5_out, not_6_out, not_7_out, not_8_out, not_9_out, or_1_out,
       or_2_out, or_3_out, or_4_out, or_5_out, or_6_out, or_7_out, or_8_out;

  not not_1 (not_1_out, EN_LO);
  not not_2 (not_2_out, not_1_out);
  and and_1 (and_1_out, not_1_out, D[0]);
  or or_1 (or_1_out, and_1_out, and_2_out);
  and and_2 (and_2_out, not_2_out, Y[0]);
  D_Flip_Flop d_ff_1 (.D(or_1_out), .clk(CP_RE), .Q(Y[0]));  // open: Qn, preset, reset
  not not_3 (not_3_out, not_1_out);
  and and_3 (and_3_out, not_1_out, D[1]);
  and and_4 (and_4_out, not_3_out, Y[1]);
  or or_2 (or_2_out, and_3_out, and_4_out);
  D_Flip_Flop d_ff_2 (.D(or_2_out), .clk(CP_RE), .Q(Y[1]));  // open: Qn, preset, reset
  and and_5 (and_5_out, not_1_out, D[2]);
  not not_4 (not_4_out, not_1_out);
  and and_6 (and_6_out, not_4_out, Y[2]);
  or or_3 (or_3_out, and_5_out, and_6_out);
  D_Flip_Flop d_ff_3 (.D(or_3_out), .clk(CP_RE), .Q(Y[2]));  // open: Qn, preset, reset
  not not_5 (not_5_out, not_1_out);
  and and_7 (and_7_out, not_1_out, D[3]);
  and and_8 (and_8_out, not_5_out, Y[3]);
  or or_4 (or_4_out, and_7_out, and_8_out);
  D_Flip_Flop d_ff_4 (.D(or_4_out), .clk(CP_RE), .Q(Y[3]));  // open: Qn, preset, reset
  not not_6 (not_6_out, not_1_out);
  and and_9 (and_9_out, not_1_out, D[4]);
  and and_10 (and_10_out, not_6_out, Y[4]);
  or or_5 (or_5_out, and_9_out, and_10_out);
  D_Flip_Flop d_ff_5 (.D(or_5_out), .clk(CP_RE), .Q(Y[4]));  // open: Qn, preset, reset
  and and_11 (and_11_out, not_1_out, D[5]);
  or or_6 (or_6_out, and_11_out, and_12_out);
  not not_7 (not_7_out, not_1_out);
  and and_12 (and_12_out, not_7_out, Y[5]);
  D_Flip_Flop d_ff_6 (.D(or_6_out), .clk(CP_RE), .Q(Y[5]));  // open: Qn, preset, reset
  not not_8 (not_8_out, not_1_out);
  and and_13 (and_13_out, not_8_out, Y[6]);
  and and_14 (and_14_out, not_1_out, D[6]);
  or or_7 (or_7_out, and_14_out, and_13_out);
  D_Flip_Flop d_ff_7 (.D(or_7_out), .clk(CP_RE), .Q(Y[6]));  // open: Qn, preset, reset
  and and_15 (and_15_out, not_1_out, D[7]);
  not not_9 (not_9_out, not_1_out);
  and and_16 (and_16_out, not_9_out, Y[7]);
  or or_8 (or_8_out, and_15_out, and_16_out);
  D_Flip_Flop d_ff_8 (.D(or_8_out), .clk(CP_RE), .Q(Y[7]));  // open: Qn, preset, reset
endmodule

// 74HC574
module EightBitRegister (
  input  [7:0] D,
  input  CP_RE,
  input  OE_LO,
  output [7:0] Y
);

  wire d_ff_1_q, d_ff_2_q, d_ff_3_q, d_ff_4_q, d_ff_5_q, d_ff_6_q, d_ff_7_q, d_ff_8_q, not_1_out;

  D_Flip_Flop d_ff_1 (.D(D[0]), .clk(CP_RE), .Q(d_ff_1_q));  // open: Qn, preset, reset
  not not_1 (not_1_out, OE_LO);
  D_Flip_Flop d_ff_2 (.D(D[1]), .clk(CP_RE), .Q(d_ff_2_q));  // open: Qn, preset, reset
  assign Y[0] = not_1_out ? d_ff_1_q : 1'bz;  // Controlled_Buffer controlled_buffer_1
  assign Y[1] = not_1_out ? d_ff_2_q : 1'bz;  // Controlled_Buffer controlled_buffer_2
  D_Flip_Flop d_ff_3 (.D(D[2]), .clk(CP_RE), .Q(d_ff_3_q));  // open: Qn, preset, reset
  D_Flip_Flop d_ff_4 (.D(D[3]), .clk(CP_RE), .Q(d_ff_4_q));  // open: Qn, preset, reset
  assign Y[2] = not_1_out ? d_ff_3_q : 1'bz;  // Controlled_Buffer controlled_buffer_3
  assign Y[3] = not_1_out ? d_ff_4_q : 1'bz;  // Controlled_Buffer controlled_buffer_4
  D_Flip_Flop d_ff_5 (.D(D[4]), .clk(CP_RE), .Q(d_ff_5_q));  // open: Qn, preset, reset
  assign Y[4] = not_1_out ? d_ff_5_q : 1'bz;  // Controlled_Buffer controlled_buffer_5
  D_Flip_Flop d_ff_6 (.D(D[5]), .clk(CP_RE), .Q(d_ff_6_q));  // open: Qn, preset, reset
  D_Flip_Flop d_ff_7 (.D(D[6]), .clk(CP_RE), .Q(d_ff_7_q));  // open: Qn, preset, reset
  assign Y[5] = not_1_out ? d_ff_6_q : 1'bz;  // Controlled_Buffer controlled_buffer_6
  assign Y[6] = not_1_out ? d_ff_7_q : 1'bz;  // Controlled_Buffer controlled_buffer_7
  D_Flip_Flop d_ff_8 (.D(D[7]), .clk(CP_RE), .Q(d_ff_8_q));  // open: Qn, preset, reset
  assign Y[7] = not_1_out ? d_ff_8_q : 1'bz;  // Controlled_Buffer controlled_buffer_8
endmodule

// 74HC161
module FourBitCounter (
  input  [3:0] D,
  input  CET_HI,
  input  CEP_HI,
  input  PE_LO,
  input  CP_FE,
  input  RST_LO,
  output TC,
  output [3:0] Y
);

  wire and_1_out, and_2_out, and_3_out, and_4_out, and_5_out, and_6_out, and_7_out, and_8_out, and_9_out,
       d_ff_1_q, d_ff_1_qn, d_ff_2_q, d_ff_2_qn, d_ff_3_q, d_ff_3_qn, d_ff_4_q, d_ff_4_qn, nand_1_out,
       nand_2_out, nor_1_out, nor_2_out, nor_3_out, nor_4_out, nor_5_out, nor_6_out, nor_7_out, nor_8_out,
       nor_9_out, not_1_out, not_2_out, not_3_out, not_4_out, not_5_out, not_7_out, not_9_out, not_10_out,
       or_1_out, xnor_1_out, xnor_2_out, xnor_3_out;

  nand nand_1 (nand_1_out, CET_HI, CEP_HI);
  not not_1 (not_1_out, PE_LO);
  not not_2 (not_2_out, not_1_out);
  nor nor_1 (nor_1_out, nand_1_out, nand_1_out);
  xnor xnor_1 (xnor_1_out, nor_1_out, d_ff_1_qn);
  and and_1 (and_1_out, D[3], not_1_out);
  and and_2 (and_2_out, xnor_1_out, not_2_out);
  nor nor_2 (nor_2_out, and_1_out, and_2_out);
  not not_3 (not_3_out, nor_2_out);
  D_Flip_Flop d_ff_1 (.D(not_3_out), .clk(not_4_out), .Q(d_ff_1_q), .Qn(d_ff_1_qn), .reset(not_5_out));  // open: preset
  not not_4 (not_4_out, CP_FE);
  not not_5 (not_5_out, RST_LO);
  not not_6 (Y[0], d_ff_1_qn);
  nor nor_3 (nor_3_out, d_ff_1_qn, nand_1_out);
  xnor xnor_2 (xnor_2_out, nor_3_out, d_ff_2_qn);
  and and_3 (and_3_out, D[2], not_1_out);
  and and_4 (and_4_out, xnor_2_out, not_2_out);
  nor nor_4 (nor_4_out, and_3_out, and_4_out);
  not not_7 (not_7_out, nor_4_out);
  D_Flip_Flop d_ff_2 (.D(not_7_out), .clk(not_4_out), .Q(d_ff_2_q), .Qn(d_ff_2_qn), .reset(not_5_out));  // open: preset
  and and_5 (and_5_out, D[1], not_1_out);
  not not_8 (Y[1], d_ff_2_qn);
  nor nor_5 (nor_5_out, d_ff_1_qn, d_ff_2_qn, nand_1_out);
  xnor xnor_3 (xnor_3_out, nor_5_out, d_ff_3_qn);
  and and_6 (and_6_out, xnor_3_out, not_2_out);
  nor nor_6 (nor_6_out, and_5_out, and_6_out);
  not not_9 (not_9_out, nor_6_out);
  D_Flip_Flop d_ff_3 (.D(not_9_out), .clk(not_4_out), .Q(d_ff_3_q), .Qn(d_ff_3_qn), .reset(not_5_out));  // open: preset
  nor nor_7 (nor_7_out, d_ff_1_qn, d_ff_2_qn, d_ff_3_qn, nand_1_out);
  nor nor_8 (nor_8_out, nor_7_out, d_ff_4_qn);
  or or_1 (or_1_out, nor_8_out, and_8_out);
  and and_7 (and_7_out, D[0], not_1_out);
  nor nor_9 (nor_9_out, and_7_out, and_9_out);
  not not_10 (not_10_out, nor_9_out);
  not not_11 (Y[2], d_ff_3_qn);
  and and_8 (and_8_out, nor_7_out, d_ff_4_qn);
  and and_9 (and_9_out, or_1_out, not_2_out);
  D_Flip_Flop d_ff_4 (
    .D(not_10_out), .clk(not_4_out), .Q(d_ff_4_q), .Qn(d_ff_4_qn), .reset(not_5_out));  // open: preset
  not not_12 (Y[3], d_ff_4_qn);
  nand nand_2 (nand_2_out, d_ff_4_q, d_ff_3_q, d_ff_2_q, d_ff_1_q, CET_HI);
  not not_13 (TC, nand_2_out);
endmodule

// 74HC138
module EightOneDecoder (
  input  A0,
  input  A1,
  input  A2,
  input  G0_LO,
  input  G1_LO,
  input  G2_HI,
  output Y0,
  output Y1,
  output Y2,
  output Y3,
  output Y4,
  output Y5,
  output Y6,
  output Y7
);

  wire and_1_out, and_2_out, and_3_out, and_4_out, and_5_out, and_6_out, and_7_out, and_8_out, and_9_out,
       not_1_out, not_2_out, not_3_out, not_4_out, not_5_out;

  not not_1 (not_1_out, A0);
  not not_2 (not_2_out, A2);
  not not_3 (not_3_out, A1);
  and and_1 (and_1_out, not_4_out, not_5_out, G2_HI);
  and and_2 (and_2_out, not_2_out, not_3_out, not_1_out);
  and and_3 (and_3_out, not_2_out, not_3_out, A0);
  and and_4 (and_4_out, not_2_out, A1, not_1_out);
  and and_5 (and_5_out, not_2_out, A1, A0);
  and and_6 (and_6_out, A2, not_3_out, not_1_out);
  and and_7 (and_7_out, A2, not_3_out, A0);
  and and_8 (and_8_out, A2, A1, not_1_out);
  and and_9 (and_9_out, A2, A1, A0);
  not not_4 (not_4_out, G0_LO);
  and and_10 (Y0, and_2_out, and_1_out);
  and and_11 (Y1, and_3_out, and_1_out);
  and and_12 (Y2, and_4_out, and_1_out);
  and and_13 (Y3, and_5_out, and_1_out);
  and and_14 (Y4, and_6_out, and_1_out);
  and and_15 (Y5, and_7_out, and_1_out);
  and and_16 (Y6, and_8_out, and_1_out);
  and and_17 (Y7, and_9_out, and_1_out);
  not not_5 (not_5_out, G1_LO);
endmodule

// 74HC244
module EightBitBuffer (
  input  [7:0] D,
  input  OE_0_LO,
  input  OE_1_LO,
  output [7:0] Y
);

  wire not_1_out, not_2_out;

  assign Y[0] = not_1_out ? D[0] : 1'bz;  // Controlled_Buffer controlled_buffer_1
  assign Y[1] = not_1_out ? D[1] : 1'bz;  // Controlled_Buffer controlled_buffer_2
  assign Y[2] = not_1_out ? D[2] : 1'bz;  // Controlled_Buffer controlled_buffer_3
  assign Y[3] = not_1_out ? D[3] : 1'bz;  // Controlled_Buffer controlled_buffer_4
  not not_1 (not_1_out, OE_0_LO);
  assign Y[4] = not_2_out ? D[4] : 1'bz;  // Controlled_Buffer controlled_buffer_5
  assign Y[5] = not_2_out ? D[5] : 1'bz;  // Controlled_Buffer controlled_buffer_6
  assign Y[6] = not_2_out ? D[6] : 1'bz;  // Controlled_Buffer controlled_buffer_7
  assign Y[7] = not_2_out ? D[7] : 1'bz;  // Controlled_Buffer controlled_buffer_8
  not not_2 (not_2_out, OE_1_LO);
endmodule

// 74HC283
module Addition (
  input  [3:0] A,
  input  [3:0] B,
  input  CIN,
  output [3:0] S,
  output COUT
);

  wire and_1_out, and_2_out, and_3_out, and_4_out, and_5_out, and_6_out, and_7_out, and_8_out, and_9_out,
       and_10_out, and_11_out, and_12_out, and_13_out, and_14_out, buffer_1_out, buffer_2_out, buffer_3_out,
       buffer_4_out, nand_1_out, nand_2_out, nand_3_out, nand_4_out, nor_1_out, nor_2_out, nor_3_out,
       nor_4_out, nor_5_out, nor_6_out, nor_7_out, not_1_out, not_2_out, not_3_out, not_4_out, not_5_out,
       not_6_out;

  nor nor_1 (nor_1_out, B[0], A[0]);
  not not_1 (not_1_out, CIN);
  nand nand_1 (nand_1_out, B[0], A[0]);
  nor nor_2 (nor_2_out, B[1], A[1]);
  nand nand_2 (nand_2_out, B[1], A[1]);
  nor nor_3 (nor_3_out, B[2], A[2]);
  nand nand_3 (nand_3_out, B[2], A[2]);
  nor nor_4 (nor_4_out, B[3], A[3]);
  nand nand_4 (nand_4_out, B[3], A[3]);
  not not_2 (not_2_out, not_1_out);
  not not_3 (not_3_out, nor_1_out);
  and and_1 (and_1_out, not_3_out, nand_1_out);
  xor xor_1 (S[0], not_2_out, and_1_out);
  buf buffer_1 (buffer_1_out, nor_1_out);
  not not_4 (not_4_out, nor_2_out);
  and and_2 (and_2_out, not_1_out, nand_1_out);
  and and_3 (and_3_out, not_4_out, nand_2_out);
  nor nor_5 (nor_5_out, and_2_out, buffer_1_out);
  xor xor_2 (S[1], nor_5_out, and_3_out);
  and and_4 (and_4_out, not_1_out, nand_1_out, nand_2_out);
  and and_5 (and_5_out, nand_2_out, nor_1_out);
  nor nor_6 (nor_6_out, and_4_out, and_5_out, buffer_2_out);
  buf buffer_2 (buffer_2_out, nor_2_out);
  not not_5 (not_5_out, nor_3_out);
  and and_6 (and_6_out, not_5_out, nand_3_out);
  xor xor_3 (S[2], nor_6_out, and_6_out);
  and and_7 (and_7_out, not_1_out, nand_1_out, nand_2_out, nand_3_out);
  and and_8 (and_8_out, nand_2_out, nand_3_out, nor_1_out);
  buf buffer_3 (buffer_3_out, nor_3_out);
  not not_6 (not_6_out, nor_4_out);
  and and_9 (and_9_out, nor_2_out, nand_3_out);
  nor nor_7 (nor_7_out, and_7_out, and_8_out, and_9_out, buffer_3_out);
  xor xor_4 (S[3], nor_7_out, and_11_out);
  and and_10 (and_10_out, not_1_out, nand_1_out, nand_2_out, nand_3_out, nand_4_out);
  and and_11 (and_11_out, not_6_out, nand_4_out);
  and and_12 (and_12_out, nand_2_out, nand_3_out, nand_4_out, nor_1_out);
  and and_13 (and_13_out, nand_3_out, nand_4_out, nor_2_out);
  and and_14 (and_14_out, nand_4_out, nor_3_out);
  nor nor_8 (COUT, and_10_out, and_12_out, and_13_out, and_14_out, buffer_4_out);
  buf buffer_4 (buffer_4_out, nor_4_out);
endmodule

// 74HC86
module Eor (
  input  [3:0] A,
  input  [3:0] B,
  output [3:0] Y
);

  xor xor_1 (Y[0], A[0], B[0]);
  xor xor_2 (Y[1], A[1], B[1]);
  xor xor_3 (Y[2], A[2], B[2]);
  xor xor_4 (Y[3], A[3], B[3]);
endmodule

// 74HC70
module NotOr (
  input  [3:0] A,
  input  [3:0] B,
  output [3:0] Y
);

  nor nor_1 (Y[0], A[0], B[0]);
  nor nor_2 (Y[1], A[1], B[1]);
  nor nor_3 (Y[2], A[2], B[2]);
  nor nor_4 (Y[3], A[3], B[3]);
endmodule

module EightOneDecoderInverted (
  input  A0,
  input  A1,
  input  A2,
  input  G0_LO,
  input  G1_LO,
  input  G2_HI,
  output Y0,
  output Y1,
  output Y2,
  output Y3,
  output Y4,
  output Y5,
  output Y6,
  output Y7
);

  wire and_1_out, and_2_out, and_3_out, and_4_out, and_5_out, and_6_out, and_7_out, and_8_out, and_9_out,
       and_10_out, and_11_out, and_12_out, and_13_out, and_14_out, and_15_out, and_16_out, and_17_out,
       not_1_out, not_2_out, not_3_out, not_4_out, not_5_out;

  not not_1 (not_1_out, A0);
  not not_2 (not_2_out, A2);
  not not_3 (not_3_out, A1);
  and and_1 (and_1_out, not_4_out, not_5_out, G2_HI);
  and and_2 (and_2_out, not_2_out, not_3_out, not_1_out);
  and and_3 (and_3_out, not_2_out, not_3_out, A0);
  and and_4 (and_4_out, not_2_out, A1, not_1_out);
  and and_5 (and_5_out, not_2_out, A1, A0);
  and and_6 (and_6_out, A2, not_3_out, not_1_out);
  and and_7 (and_7_out, A2, not_3_out, A0);
  and and_8 (and_8_out, A2, A1, not_1_out);
  and and_9 (and_9_out, A2, A1, A0);
  not not_4 (not_4_out, G0_LO);
  and and_10 (and_10_out, and_2_out, and_1_out);
  and and_11 (and_11_out, and_3_out, and_1_out);
  and and_12 (and_12_out, and_4_out, and_1_out);
  and and_13 (and_13_out, and_5_out, and_1_out);
  and and_14 (and_14_out, and_6_out, and_1_out);
  and and_15 (and_15_out, and_7_out, and_1_out);
  and and_16 (and_16_out, and_8_out, and_1_out);
  and and_17 (and_17_out, and_9_out, and_1_out);
  not not_5 (not_5_out, G1_LO);
  not not_6 (Y0, and_10_out);
  not not_7 (Y1, and_11_out);
  not not_8 (Y2, and_12_out);
  not not_9 (Y3, and_13_out);
  not not_10 (Y4, and_14_out);
  not not_11 (Y5, and_15_out);
  not not_12 (Y6, and_16_out);
  not not_13 (Y7, and_17_out);
endmodule

module NotAnd (
  input  [3:0] A,
  input  [3:0] B,
  output [3:0] Y
);

  nand nand_1 (Y[0], A[0], B[0]);
  nand nand_2 (Y[1], A[1], B[1]);
  nand nand_3 (Y[2], A[2], B[2]);
  nand nand_4 (Y[3], A[3], B[3]);
endmodule

// 74HC164
module ShiftRegisterIn (
  input  DSA,
  input  DSB,
  input  CP_RE,
  input  MR_LO,
  output [7:0] Y
);

  wire and_1_out, not_1_out, not_2_out;

  D_Flip_Flop d_ff_1 (.D(and_1_out), .clk(not_1_out), .Q(Y[7]), .reset(not_2_out));  // open: Qn, preset
  and and_1 (and_1_out, DSA, DSB);
  not not_1 (not_1_out, CP_RE);
  not not_2 (not_2_out, MR_LO);
  D_Flip_Flop d_ff_2 (.D(Y[7]), .clk(not_1_out), .Q(Y[6]), .reset(not_2_out));  // open: Qn, preset
  D_Flip_Flop d_ff_3 (.D(Y[6]), .clk(not_1_out), .Q(Y[5]), .reset(not_2_out));  // open: Qn, preset
  D_Flip_Flop d_ff_4 (.D(Y[5]), .clk(not_1_out), .Q(Y[4]), .reset(not_2_out));  // open: Qn, preset
  D_Flip_Flop d_ff_5 (.D(Y[4]), .clk(not_1_out), .Q(Y[3]), .reset(not_2_out));  // open: Qn, preset
  D_Flip_Flop d_ff_6 (.D(Y[3]), .clk(not_1_out), .Q(Y[2]), .reset(not_2_out));  // open: Qn, preset
  D_Flip_Flop d_ff_7 (.D(Y[2]), .clk(not_1_out), .Q(Y[1]), .reset(not_2_out));  // open: Qn, preset
  D_Flip_Flop d_ff_8 (.D(Y[1]), .clk(not_1_out), .Q(Y[0]), .reset(not_2_out));  // open: Qn, preset
endmodule

// 74HC165
module ShiftRegisterOut (
  input  [7:0] P,
  input  S_IN,
  input  CLK_INH,
  input  SH_HI_LD_LO,
  input  CLK_HI,
  output Q,
  output Q_BAR
);

  _74165 u_74165_1 (
    .pin1(SH_HI_LD_LO), .pin2(CLK_HI), .pin3(P[4]), .pin4(P[5]), .pin5(P[6]), .pin6(P[7]), .pin7(Q_BAR),
    .pin15(CLK_INH), .pin14(P[3]), .pin13(P[2]), .pin12(P[1]), .pin11(P[0]), .pin10(S_IN), .pin9(Q));
endmodule
