// Logisim project SAM.circ as structural Verilog: 9 circuits, main circuit CPU
module CPU (
  input  CLK,
  input  RST_LO,
  input  MISO,
  output [7:0] DS,
  output MOSI,
  output SCLK
);

  wire pull_resistor_1_node, pull_resistor_2_node;
  wire [11:0] alu_1_cout;
  wire [15:0] alu_1_arr, LHS_IMM_out_4, mainmemory_1_data_out, MAR_y, PC_y, RHS_IMM_out_4;
  wire [30:0] microcodeengine_1_y;

  ImmediateGenerator LHS_IMM (
    .IMM_0(microcodeengine_1_y[13]), .IMM_Sign(microcodeengine_1_y[14]), .OE_LO(microcodeengine_1_y[15]),
    .out_4(LHS_IMM_out_4));
  Register16bit AC (.D(alu_1_arr), .CP_RE(microcodeengine_1_y[16]), .OE_LO(microcodeengine_1_y[17]), .Y(LHS_IMM_out_4));
  Register16bit IX (.D(alu_1_arr), .CP_RE(microcodeengine_1_y[18]), .OE_LO(microcodeengine_1_y[19]), .Y(LHS_IMM_out_4));
  BufferedCounter16bit PC (
    .D(alu_1_arr), .CP_FE(microcodeengine_1_y[20]), .CEP_HI(microcodeengine_1_y[21]), .RST_LO(RST_LO),
    .YB_OE_LO(microcodeengine_1_y[23]), .Y(PC_y), .YB(LHS_IMM_out_4));
  Register16bit MAR (.D(alu_1_arr), .CP_RE(microcodeengine_1_y[24]), .OE_LO(microcodeengine_1_y[25]), .Y(MAR_y));
  Pull_Resistor pull_resistor_1 (.node(pull_resistor_1_node));
  // Probe on PC_y
  Pull_Resistor #(.pull(1)) pull_resistor_2 (.node(pull_resistor_2_node));
  ImmediateGenerator RHS_IMM (
    .IMM_0(pull_resistor_1_node), .IMM_Sign(pull_resistor_1_node), .OE_LO(microcodeengine_1_y[5]),
    .out_4(RHS_IMM_out_4));
  Register16bit MOR (
    .D(mainmemory_1_data_out), .CP_RE(microcodeengine_1_y[6]), .OE_LO(microcodeengine_1_y[7]),
    .Y(RHS_IMM_out_4));
  InstructionRegister IR (
    .INS_IN(mainmemory_1_data_out), .CP_RE(microcodeengine_1_y[8]), .IMM_OE_LO(microcodeengine_1_y[9]),
    .IMM(RHS_IMM_out_4), .Opcode(alu_1_cout[11:4]));
  MainMemory mainmemory_1 (
    .PC_IN(PC_y), .WE_HI(microcodeengine_1_y[10]), .IN_SEL(microcodeengine_1_y[11]),
    .OE_HI(pull_resistor_2_node), .CP_WR_RE(microcodeengine_1_y[12]), .DATA_IN(LHS_IMM_out_4),
    .MAR_IN(MAR_y), .DATA_OUT(mainmemory_1_data_out));
  // Probe on RHS_IMM_out_4
  Pull_Resistor pull_resistor_3 (.node(alu_1_cout[3]));
  ALU alu_1 (
    .A(LHS_IMM_out_4), .B(RHS_IMM_out_4), .ALU_CP_RE(microcodeengine_1_y[0]),
    .ALU_ROR_HI(microcodeengine_1_y[1]), .FN_SEL_0(microcodeengine_1_y[2]),
    .FN_SEL_1(microcodeengine_1_y[3]), .COUT_CP_RE(microcodeengine_1_y[4]), .ARR(alu_1_arr),
    .COUT(alu_1_cout[0]));
  MicroCodeEngine microcodeengine_1 (
    .I({alu_1_cout[11:3], {2{alu_1_cout[3]}}, alu_1_cout[0]}), .RST_LO(RST_LO), .CLK(CLK),
    .Y({microcodeengine_1_y[30:23], SCLK, microcodeengine_1_y[21:0]}));
  SpiEngine spiengine_1 (
    .DS_IN(RHS_IMM_out_4), .DS_CP_RE(microcodeengine_1_y[26]), .OE_LO(microcodeengine_1_y[27]), .MISO(MISO),
    .CLK_IN_RE(microcodeengine_1_y[28]), .I(LHS_IMM_out_4), .SH_HI_LD_LO(microcodeengine_1_y[29]),
    .CLK_OUT_RE(microcodeengine_1_y[30]), .DS_BAR(DS), .Y(RHS_IMM_out_4), .MOSI(MOSI));
endmodule

module Register16bit (
  input  [15:0] D,
  input  CP_RE,
  input  OE_LO,
  output [15:0] Y
);

  EightBitRegister eightbitregister_1 (.D(D[7:0]), .CP_RE(CP_RE), .OE_LO(OE_LO), .Y(Y[7:0]));
  EightBitRegister eightbitregister_2 (.D(D[15:8]), .CP_RE(CP_RE), .OE_LO(OE_LO), .Y(Y[15:8]));
endmodule

module BufferedCounter16bit (
  input  [15:0] D,
  input  CP_FE,
  input  CEP_HI,
  input  RST_LO,
  input  YB_OE_LO,
  output [15:0] Y,
  output [15:0] YB
);

  wire fourbitcounter_1_tc, fourbitcounter_2_tc, fourbitcounter_3_tc, fourbitcounter_4_tc;

  FourBitCounter fourbitcounter_1 (
    .D(D[3:0]), .CET_HI(CEP_HI), .CEP_HI(CEP_HI), .PE_LO(CEP_HI), .CP_FE(CP_FE), .RST_LO(RST_LO),
    .TC(fourbitcounter_1_tc), .Y(Y[3:0]));
  FourBitCounter fourbitcounter_2 (
    .D(D[7:4]), .CET_HI(CEP_HI), .CEP_HI(CEP_HI), .PE_LO(CEP_HI), .CP_FE(fourbitcounter_1_tc),
    .RST_LO(RST_LO), .TC(fourbitcounter_2_tc), .Y(Y[7:4]));
  FourBitCounter fourbitcounter_3 (
    .D(D[11:8]), .CET_HI(CEP_HI), .CEP_HI(CEP_HI), .PE_LO(CEP_HI), .CP_FE(fourbitcounter_2_tc),
    .RST_LO(RST_LO), .TC(fourbitcounter_3_tc), .Y(Y[11:8]));
  // NoConnect on fourbitcounter_4_tc
  FourBitCounter fourbitcounter_4 (
    .D(D[15:12]), .CET_HI(CEP_HI), .CEP_HI(CEP_HI), .PE_LO(CEP_HI), .CP_FE(fourbitcounter_3_tc),
    .RST_LO(RST_LO), .TC(fourbitcounter_4_tc), .Y(Y[15:12]));
  EightBitBuffer eightbitbuffer_1 (.D(Y[7:0]), .OE_0_LO(YB_OE_LO), .OE_1_LO(YB_OE_LO), .Y(YB[7:0]));
  EightBitBuffer eightbitbuffer_2 (.D(Y[15:8]), .OE_0_LO(YB_OE_LO), .OE_1_LO(YB_OE_LO), .Y(YB[15:8]));
endmodule

module ImmediateGenerator (
  input  IMM_0,
  input  IMM_Sign,
  input  OE_LO,
  output [15:0] out_4
);

  EightBitBuffer eightbitbuffer_1 (.D({{7{IMM_Sign}}, IMM_0}), .OE_0_LO(OE_LO), .OE_1_LO(OE_LO), .Y(out_4[7:0]));
  EightBitBuffer eightbitbuffer_2 (.D({8{IMM_Sign}}), .OE_0_LO(OE_LO), .OE_1_LO(OE_LO), .Y(out_4[15:8]));
endmodule

module InstructionRegister (
  input  [15:0] INS_IN,
  input  CP_RE,
  input  IMM_OE_LO,
  output [15:0] IMM,
  output [7:0] Opcode
);

  wire pull_resistor_1_node;
  wire [7:0] eightbitlatch_1_y;

  Pull_Resistor pull_resistor_1 (.node(pull_resistor_1_node));
  EightBitLatch eightbitlatch_1 (.D(INS_IN[7:0]), .EN_LO(pull_resistor_1_node), .CP_RE(CP_RE), .Y(eightbitlatch_1_y));
  EightBitLatch eightbitlatch_2 (.D(INS_IN[15:8]), .EN_LO(pull_resistor_1_node), .CP_RE(CP_RE), .Y(Opcode));
  EightBitBuffer eightbitbuffer_1 (.D(eightbitlatch_1_y), .OE_0_LO(IMM_OE_LO), .OE_1_LO(IMM_OE_LO), .Y(IMM[7:0]));
  EightBitBuffer eightbitbuffer_2 (
    .D({8{eightbitlatch_1_y[7]}}), .OE_0_LO(IMM_OE_LO), .OE_1_LO(IMM_OE_LO), .Y(IMM[15:8]));
endmodule

module ALU (
  input  [15:0] A,
  input  [15:0] B,
  input  ALU_CP_RE,
  input  ALU_ROR_HI,
  input  FN_SEL_0,
  input  FN_SEL_1,
  input  COUT_CP_RE,
  output [15:0] ARR,
  output COUT
);

  wire addition_1_cout, addition_2_cout, addition_3_cout, eightonedecoderinverted_1_y2,
       eightonedecoderinverted_1_y3, not_1_out, pull_resistor_1_node, pull_resistor_2_node,
       pull_resistor_4_node, pull_resistor_5_node;
  wire [0:0] eightonedecoderinverted_1_y1;
  wire [3:0] eor_1_y, eor_2_y, eor_3_y, eor_4_y, eor_5_y, eor_6_y, eor_7_y, eor_8_y, notor_1_y, notor_2_y,
       notor_3_y, notor_4_y;
  wire [3:1] notand_1_y, pull_resistor_3_node;
  wire [3:3] eightonedecoderinverted_1_y0;
  wire [6:0] eightbitlatch_1_y;
  wire [7:0] eightbitbuffer_1_y, eightbitbuffer_2_y, eightbitlatch_2_y, eightbitlatch_3_y, undriven;
  wire [15:0] addition_1_s;

  Pull_Resistor pull_resistor_1 (.node(pull_resistor_1_node));
  Pull_Resistor #(.pull(1)) pull_resistor_2 (.node(pull_resistor_2_node));
  EightOneDecoderInverted eightonedecoderinverted_1 (
    .A0(FN_SEL_0), .A1(FN_SEL_1), .A2(pull_resistor_1_node), .G0_LO(pull_resistor_1_node),
    .G1_LO(pull_resistor_1_node), .G2_HI(pull_resistor_2_node), .Y0(eightonedecoderinverted_1_y0[3]),
    .Y1(eightonedecoderinverted_1_y1[0]), .Y2(eightonedecoderinverted_1_y2), .Y3(eightonedecoderinverted_1_y3));  // open: Y4, Y5, Y6, Y7
  Eor eor_1 (.A(B[3:0]), .B({4{eightonedecoderinverted_1_y0[3]}}), .Y(eor_1_y));
  Eor eor_2 (.A(B[7:4]), .B({4{eightonedecoderinverted_1_y0[3]}}), .Y(eor_2_y));
  Eor eor_3 (.A(B[11:8]), .B({4{eightonedecoderinverted_1_y0[3]}}), .Y(eor_3_y));
  Eor eor_4 (.A(B[15:12]), .B({4{eightonedecoderinverted_1_y0[3]}}), .Y(eor_4_y));
  Pull_Resistor pull_resistor_3 (.node(pull_resistor_3_node[3]));
  Addition addition_1 (
    .A(A[3:0]), .B(eor_1_y), .CIN(eightonedecoderinverted_1_y0[3]), .S(addition_1_s[3:0]),
    .COUT(addition_1_cout));
  Addition addition_2 (.A(A[7:4]), .B(eor_2_y), .CIN(addition_1_cout), .S(addition_1_s[7:4]), .COUT(addition_2_cout));
  Addition addition_3 (.A(A[11:8]), .B(eor_3_y), .CIN(addition_2_cout), .S(addition_1_s[11:8]), .COUT(addition_3_cout));
  Addition addition_4 (.A(A[15:12]), .B(eor_4_y), .CIN(addition_3_cout), .S(addition_1_s[15:12]), .COUT(undriven[7]));
  // NoConnect on notand_1_y[2]
  // NoConnect on notand_1_y[3]
  NotAnd notand_1 (
    .A({{2{pull_resistor_3_node[3]}}, pull_resistor_3_node[1], eightonedecoderinverted_1_y0[3]}),
    .B({{2{pull_resistor_3_node[3]}}, pull_resistor_3_node[1], eightonedecoderinverted_1_y1[0]}),
    .Y({notand_1_y, pull_resistor_3_node[1]}));
  Pull_Resistor pull_resistor_4 (.node(pull_resistor_4_node));
  // Probe on {eightbitbuffer_2_y, eightbitbuffer_1_y}
  EightBitBuffer eightbitbuffer_1 (
    .D(addition_1_s[7:0]), .OE_0_LO(notand_1_y[1]), .OE_1_LO(notand_1_y[1]), .Y(eightbitbuffer_1_y));
  EightBitBuffer eightbitbuffer_2 (
    .D(addition_1_s[15:8]), .OE_0_LO(notand_1_y[1]), .OE_1_LO(notand_1_y[1]), .Y(eightbitbuffer_2_y));
  EightBitLatch eightbitlatch_1 (
    .D(undriven), .EN_LO(pull_resistor_4_node), .CP_RE(COUT_CP_RE), .Y({COUT, eightbitlatch_1_y}));
  NotOr notor_1 (.A(B[3:0]), .B(A[3:0]), .Y(notor_1_y));
  NotOr notor_2 (.A(B[7:4]), .B(A[7:4]), .Y(notor_2_y));
  NotOr notor_3 (.A(B[11:8]), .B(A[11:8]), .Y(notor_3_y));
  NotOr notor_4 (.A(B[15:12]), .B(A[15:12]), .Y(notor_4_y));
  EightBitBuffer eightbitbuffer_3 (
    .D({notor_2_y, notor_1_y}), .OE_0_LO(eightonedecoderinverted_1_y2),
    .OE_1_LO(eightonedecoderinverted_1_y2), .Y(eightbitbuffer_1_y));
  EightBitBuffer eightbitbuffer_4 (
    .D({notor_4_y, notor_3_y}), .OE_0_LO(eightonedecoderinverted_1_y2),
    .OE_1_LO(eightonedecoderinverted_1_y2), .Y(eightbitbuffer_2_y));
  Eor eor_5 (.A(B[3:0]), .B(A[3:0]), .Y(eor_5_y));
  Eor eor_6 (.A(B[7:4]), .B(A[7:4]), .Y(eor_6_y));
  Eor eor_7 (.A(B[11:8]), .B(A[11:8]), .Y(eor_7_y));
  Eor eor_8 (.A(B[15:12]), .B(A[15:12]), .Y(eor_8_y));
  EightBitBuffer eightbitbuffer_5 (
    .D({eor_6_y, eor_5_y}), .OE_0_LO(eightonedecoderinverted_1_y3), .OE_1_LO(eightonedecoderinverted_1_y3),
    .Y(eightbitbuffer_1_y));
  EightBitBuffer eightbitbuffer_6 (
    .D({eor_8_y, eor_7_y}), .OE_0_LO(eightonedecoderinverted_1_y3), .OE_1_LO(eightonedecoderinverted_1_y3),
    .Y(eightbitbuffer_2_y));
  Pull_Resistor pull_resistor_5 (.node(pull_resistor_5_node));
  EightBitLatch eightbitlatch_2 (
    .D(eightbitbuffer_1_y), .EN_LO(pull_resistor_5_node), .CP_RE(ALU_CP_RE), .Y(eightbitlatch_2_y));
  EightBitLatch eightbitlatch_3 (
    .D(eightbitbuffer_2_y), .EN_LO(pull_resistor_5_node), .CP_RE(ALU_CP_RE), .Y(eightbitlatch_3_y));
  not not_1 (not_1_out, ALU_ROR_HI);
  EightBitBuffer eightbitbuffer_7 (.D(eightbitlatch_2_y), .OE_0_LO(ALU_ROR_HI), .OE_1_LO(ALU_ROR_HI), .Y(ARR[7:0]));
  EightBitBuffer eightbitbuffer_8 (.D(eightbitlatch_3_y), .OE_0_LO(ALU_ROR_HI), .OE_1_LO(ALU_ROR_HI), .Y(ARR[15:8]));
  EightBitBuffer eightbitbuffer_9 (
    .D({eightbitlatch_2_y[7:1], eightbitlatch_3_y[7]}), .OE_0_LO(not_1_out), .OE_1_LO(not_1_out), .Y(ARR[7:0]));
  EightBitBuffer eightbitbuffer_10 (
    .D({eightbitlatch_2_y[0], eightbitlatch_3_y[6:0]}), .OE_0_LO(not_1_out), .OE_1_LO(not_1_out),
    .Y(ARR[15:8]));
endmodule

module MainMemory (
  input  [15:0] PC_IN,
  input  WE_HI,
  input  IN_SEL,
  input  OE_HI,
  input  CP_WR_RE,
  input  [15:0] DATA_IN,
  input  [15:0] MAR_IN,
  output [15:0] DATA_OUT
);

  wire nand_1_out;
  wire [7:0] eightbitbuffer_1_y, eightbitbuffer_2_y;

  nand nand_1 (nand_1_out, IN_SEL, IN_SEL);
  EightBitBuffer eightbitbuffer_1 (.D(PC_IN[7:0]), .OE_0_LO(IN_SEL), .OE_1_LO(IN_SEL), .Y(eightbitbuffer_1_y));
  EightBitBuffer eightbitbuffer_2 (.D(PC_IN[15:8]), .OE_0_LO(IN_SEL), .OE_1_LO(IN_SEL), .Y(eightbitbuffer_2_y));
  EightBitBuffer eightbitbuffer_3 (.D(MAR_IN[7:0]), .OE_0_LO(nand_1_out), .OE_1_LO(nand_1_out), .Y(eightbitbuffer_1_y));
  EightBitBuffer eightbitbuffer_4 (
    .D(MAR_IN[15:8]), .OE_0_LO(nand_1_out), .OE_1_LO(nand_1_out), .Y(eightbitbuffer_2_y));
  RAM #(.addrWidth(16), .asyncread("true"), .dataWidth(16)) ram_1 (
    .addr({eightbitbuffer_2_y, eightbitbuffer_1_y}), .we(WE_HI), .oe(OE_HI), .clk(CP_WR_RE), .din(DATA_IN),
    .dout(DATA_OUT));
endmodule

module MicroCodeEngine (
  input  [11:0] I,
  input  RST_LO,
  input  CLK,
  output [30:0] Y
);

  wire and_1_out, fourbitcounter_1_tc, pull_resistor_1_node, pull_resistor_2_node;
  wire [3:0] fourbitcounter_1_y, undriven;
  wire [7:7] eightbitlatch_4_y;
  wire [31:0] rom_1_data;

  // NoConnect on undriven
  Pull_Resistor #(.pull(1)) pull_resistor_1 (.node(pull_resistor_1_node));
  and and_1 (and_1_out, RST_LO, eightbitlatch_4_y[7]);
  // NoConnect on fourbitcounter_1_tc
  FourBitCounter fourbitcounter_1 (
    .D(undriven), .CET_HI(pull_resistor_1_node), .CEP_HI(pull_resistor_1_node), .PE_LO(pull_resistor_1_node),
    .CP_FE(CLK), .RST_LO(and_1_out), .TC(fourbitcounter_1_tc), .Y(fourbitcounter_1_y));
  ROM #(.addrWidth(16), .dataWidth(32)) rom_1 (.addr({I, fourbitcounter_1_y}), .data(rom_1_data));
  // Probe on rom_1_data
  Pull_Resistor pull_resistor_2 (.node(pull_resistor_2_node));
  EightBitLatch eightbitlatch_1 (.D(rom_1_data[7:0]), .EN_LO(pull_resistor_2_node), .CP_RE(CLK), .Y(Y[7:0]));
  EightBitLatch eightbitlatch_2 (.D(rom_1_data[15:8]), .EN_LO(pull_resistor_2_node), .CP_RE(CLK), .Y(Y[15:8]));
  EightBitLatch eightbitlatch_3 (.D(rom_1_data[23:16]), .EN_LO(pull_resistor_2_node), .CP_RE(CLK), .Y(Y[23:16]));
  EightBitLatch eightbitlatch_4 (
    .D(rom_1_data[31:24]), .EN_LO(pull_resistor_2_node), .CP_RE(CLK), .Y({eightbitlatch_4_y[7], Y[30:24]}));

  // Notes on the sheet:
  //   contents of rom_1 (hex, n*v repeats v):
  //   aa8ea3a0 aa8aa2a0 14*aa86a2a0 aa8ea3a0 aa8aa2a0 238*aa86a2a0 aa8ea3a0 aa8aa2a0 14*aa86a2a0 aa8ea3a0
  //   aa8aa2a0 238*aa86a2a0 aa8ea3a0 aa8aa2a0 14*aa86a2a0 aa8ea3a0 aa8aa2a0 238*aa86a2a0 aa8ea3a0 aa8aa2a0
  //   14*aa86a2a0 aa8ea3a0 aa8aa2a0 238*aa86a2a0 aa8ea3a0 aa8aa2a0 aa8680a0 aa8680a1 2a86e2a0 11*aa86a2a0
  //   aa8ea3a0 aa8aa2a0 aa8680a0 aa8680a1 2a86e2a0 235*aa86a2a0 aa8ea3a0 aa8aa2a0 aa8620a0 aa8620a1
  //   2a86e2a0 11*aa86a2a0 aa8ea3a0 aa8aa2a0 aa8620a0 aa8620a1 2a86e2a0 235*aa86a2a0 aa8ea3a0 aa8aa2a0
  //   aa84a0a0 aa84a0a1 2a86e2a0 11*aa86a2a0 aa8ea3a0 aa8aa2a0 aa84a0a0 aa84a0a1 2a86e2a0 235*aa86a2a0
  //   aa8ea3a0 aa8aa2a0 aa06a0a0 aa06a0a1 2a86e2a0 11*aa86a2a0 aa8ea3a0 aa8aa2a0 aa06a0a0 aa06a0a1
  //   2a86e2a0 235*aa86a2a0 aa8ea3a0 aa8aa2a0 aa8680a0 aa8680a1 2a87a2a0 11*aa86a2a0 aa8ea3a0 aa8aa2a0
  //   aa8680a0 aa8680a1 2a87a2a0 235*aa86a2a0 aa8ea3a0 aa8aa2a0 aa8620a0 aa8620a1 2a87a2a0 11*aa86a2a0
  //   aa8ea3a0 aa8aa2a0 aa8620a0 aa8620a1 2a87a2a0 235*aa86a2a0 aa8ea3a0 aa8aa2a0 aa84a0a0 aa84a0a1
  //   2a87a2a0 11*aa86a2a0 aa8ea3a0 aa8aa2a0 aa84a0a0 aa84a0a1 2a87a2a0 235*aa86a2a0 aa8ea3a0 aa8aa2a0
  //   aa06a0a0 aa06a0a1 2a87a2a0 11*aa86a2a0 aa8ea3a0 aa8aa2a0 aa06a0a0 aa06a0a1 2a87a2a0 235*aa86a2a0
  //   aa8ea3a0 aa8aa2a0 aa8680a0 aa8680a1 2a82a2a0 11*aa86a2a0 aa8ea3a0 aa8aa2a0 aa8680a0 aa8680a1
  //   2a82a2a0 235*aa86a2a0 aa8ea3a0 aa8aa2a0 aa8620a0 aa8620a1 2a82a2a0 11*aa86a2a0 aa8ea3a0 aa8aa2a0
  //   aa8620a0 aa8620a1 2a82a2a0 235*aa86a2a0 aa8ea3a0 aa8aa2a0 aa84a0a0 aa84a0a1 2a82a2a0 11*aa86a2a0
  //   aa8ea3a0 aa8aa2a0 aa84a0a0 aa84a0a1 2a82a2a0 235*aa86a2a0 aa8ea3a0 aa8aa2a0 aa06a0a0 aa06a0a1
  //   2a82a2a0 11*aa86a2a0 aa8ea3a0 aa8aa2a0 aa06a0a0 aa06a0a1 2a82a2a0 235*aa86a2a0 aa8ea3a0 aa8aa2a0
  //   14*aa86a2a0 aa8ea3a0 aa8aa2a0 238*aa86a2a0 aa8ea3a0 aa8aa2a0 14*aa86a2a0 aa8ea3a0 aa8aa2a0
  //   238*aa86a2a0 aa8ea3a0 aa8aa2a0 14*aa86a2a0 aa8ea3a0 aa8aa2a0 238*aa86a2a0 aa8ea3a0 aa8aa2a0
  //   14*aa86a2a0 aa8ea3a0 aa8aa2a0 238*aa86a2a0 aa8ea3a0 aa8aa2a0 aa8ea3a0 aa8aa2a0 12*aa86a2a0 aa8ea3a0
  //   aa8aa2a0 aa8680a0 aa8680a1 2a86e2a0 235*aa86a2a0 aa8ea3a0 aa8aa2a0 aa8ea3a0 aa8aa2a0 12*aa86a2a0
  //   aa8ea3a0 aa8aa2a0 aa8620a0 aa8620a1 2a86e2a0 235*aa86a2a0 aa8ea3a0 aa8aa2a0 aa8ea3a0 aa8aa2a0
  //   12*aa86a2a0 aa8ea3a0 aa8aa2a0 aa84a0a0 aa84a0a1 2a86e2a0 235*aa86a2a0 aa8ea3a0 aa8aa2a0 aa8ea3a0
  //   aa8aa2a0 12*aa86a2a0 aa8ea3a0 aa8aa2a0 aa06a0a0 aa06a0a1 2a86e2a0 235*aa86a2a0 aa8ea3a0 aa8aa2a0
  //   aa8ea3a0 aa8aa2a0 12*aa86a2a0 aa8ea3a0 aa8aa2a0 aa8680a0 aa8680a1 2a87a2a0 235*aa86a2a0 aa8ea3a0
  //   aa8aa2a0 aa8ea3a0 aa8aa2a0 12*aa86a2a0 aa8ea3a0 aa8aa2a0 aa8620a0 aa8620a1 2a87a2a0 235*aa86a2a0
  //   aa8ea3a0 aa8aa2a0 aa8ea3a0 aa8aa2a0 12*aa86a2a0 aa8ea3a0 aa8aa2a0 aa84a0a0 aa84a0a1 2a87a2a0
  //   235*aa86a2a0 aa8ea3a0 aa8aa2a0 aa8ea3a0 aa8aa2a0 12*aa86a2a0 aa8ea3a0 aa8aa2a0 aa06a0a0 aa06a0a1
  //   2a87a2a0 235*aa86a2a0 aa8ea3a0 aa8aa2a0 aa8ea3a0 aa8aa2a0 12*aa86a2a0 aa8ea3a0 aa8aa2a0 aa8680a0
  //   aa8680a1 2a82a2a0 235*aa86a2a0 aa8ea3a0 aa8aa2a0 aa8ea3a0 aa8aa2a0 12*aa86a2a0 aa8ea3a0 aa8aa2a0
  //   aa8620a0 aa8620a1 2a82a2a0 235*aa86a2a0 aa8ea3a0 aa8aa2a0 aa8ea3a0 aa8aa2a0 12*aa86a2a0 aa8ea3a0
  //   aa8aa2a0 aa84a0a0 aa84a0a1 2a82a2a0 235*aa86a2a0 aa8ea3a0 aa8aa2a0 aa8ea3a0 aa8aa2a0 12*aa86a2a0
  //   aa8ea3a0 aa8aa2a0 aa06a0a0 aa06a0a1 2a82a2a0 235*aa86a2a0 aa8ea3a0 aa8aa2a0 14*aa86a2a0 aa8ea3a0
  //   aa8aa2a0 238*aa86a2a0 aa8ea3a0 aa8aa2a0 14*aa86a2a0 aa8ea3a0 aa8aa2a0 238*aa86a2a0 aa8ea3a0 aa8aa2a0
  //   14*aa86a2a0 aa8ea3a0 aa8aa2a0 238*aa86a2a0 aa8ea3a0 aa8aa2a0 14*aa86a2a0 aa8ea3a0 aa8aa2a0
  //   238*aa86a2a0 aa8ea3a0 aa8aa2a0 14*aa86a2a0 aa8ea3a0 aa8aa2a0 238*aa86a2a0 aa8ea3a0 aa8aa2a0
  //   14*aa86a2a0 aa8ea3a0 aa8aa2a0 238*aa86a2a0 aa8ea3a0 aa8aa2a0 14*aa86a2a0 aa8ea3a0 aa8aa2a0
  //   238*aa86a2a0 aa8ea3a0 aa8aa2a0 14*aa86a2a0 aa8ea3a0 aa8aa2a0 238*aa86a2a0 aa8ea3a0 aa8aa2a0
  //   14*aa86a2a0 aa8ea3a0 aa8aa2a0 238*aa86a2a0 aa8ea3a0 aa8aa2a0 14*aa86a2a0 aa8ea3a0 aa8aa2a0
  //   238*aa86a2a0 aa8ea3a0 aa8aa2a0 14*aa86a2a0 aa8ea3a0 aa8aa2a0 238*aa86a2a0 aa8ea3a0 aa8aa2a0
  //   14*aa86a2a0 aa8ea3a0 aa8aa2a0 238*aa86a2a0 aa8ea3a0 aa8aa2a0 14*aa86a2a0 aa8ea3a0 aa8aa2a0
  //   238*aa86a2a0 aa8ea3a0 aa8aa2a0 14*aa86a2a0 aa8ea3a0 aa8aa2a0 238*aa86a2a0 aa8ea3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
endmodule

module SpiEngine (
  input  [15:0] DS_IN,
  input  DS_CP_RE,
  input  OE_LO,
  input  MISO,
  input  CLK_IN_RE,
  input  [15:0] I,
  input  SH_HI_LD_LO,
  input  CLK_OUT_RE,
  output [7:0] DS_BAR,
  output [15:0] Y,
  output MOSI
);

  wire pull_resistor_1_node, pull_resistor_2_node, pull_resistor_3_node, pull_resistor_4_node,
       pull_resistor_5_node;
  wire [7:0] eightbitlatch_1_y, pull_resistor_6_node, shiftregisterin_1_y;

  // NoConnect on DS_IN[15:8]
  Pull_Resistor pull_resistor_1 (.node(pull_resistor_1_node));
  EightBitLatch eightbitlatch_1 (.D(DS_IN[7:0]), .EN_LO(pull_resistor_1_node), .CP_RE(DS_CP_RE), .Y(eightbitlatch_1_y));
  Pull_Resistor pull_resistor_2 (.node(pull_resistor_2_node));
  Pull_Resistor pull_resistor_3 (.node(pull_resistor_3_node));
  Pull_Resistor #(.pull(1)) pull_resistor_4 (.node(pull_resistor_4_node));
  Pull_Resistor #(.pull(1)) pull_resistor_5 (.node(pull_resistor_5_node));
  // NoConnect on I[15:8]
  EightOneDecoderInverted eightonedecoderinverted_1 (
    .A0(eightbitlatch_1_y[0]), .A1(eightbitlatch_1_y[1]), .A2(eightbitlatch_1_y[2]),
    .G0_LO(pull_resistor_3_node), .G1_LO(pull_resistor_3_node), .G2_HI(pull_resistor_4_node), .Y0(DS_BAR[0]),
    .Y1(DS_BAR[1]), .Y2(DS_BAR[2]), .Y3(DS_BAR[3]), .Y4(DS_BAR[4]), .Y5(DS_BAR[5]), .Y6(DS_BAR[6]),
    .Y7(DS_BAR[7]));
  Pull_Resistor pull_resistor_6 (.node(pull_resistor_6_node));
  ShiftRegisterIn shiftregisterin_1 (
    .DSA(MISO), .DSB(MISO), .CP_RE(CLK_IN_RE), .MR_LO(pull_resistor_5_node), .Y(shiftregisterin_1_y));
  ShiftRegisterOut shiftregisterout_1 (
    .P(I[7:0]), .S_IN(pull_resistor_2_node), .CLK_INH(pull_resistor_2_node), .SH_HI_LD_LO(SH_HI_LD_LO),
    .CLK_HI(CLK_OUT_RE), .Q(MOSI));  // open: Q_BAR
  EightBitBuffer eightbitbuffer_1 (.D(pull_resistor_6_node), .OE_0_LO(OE_LO), .OE_1_LO(OE_LO), .Y(Y[7:0]));
  EightBitBuffer eightbitbuffer_2 (.D(shiftregisterin_1_y), .OE_0_LO(OE_LO), .OE_1_LO(OE_LO), .Y(Y[15:8]));
endmodule
